# Fritzing sketch marax_monitor_circuit_board (saved by Fritzing 0.9.3b)
circuit board: 12.104cm x 6.6451cm
breadboards: 1

parts:
  ESP8266_NodeMCU_1_0 = NodeMCU V1.0
  BS = WeMos D1 Mini Battery Shield
  PNP_IRF9540N = Basic FET P-Channel [package="TO220 [THT]"]
  NPN_2N7000 = MOSFET-NCHANNEL [package=to-92]
  5k = Resistor [tolerance=±5% resistance=5k package=THT]
  Pushbttn = Pushbutton [package=THT]
  D1 = Zener Diode [part_number=1N4732A breakdown_voltage=3.6V package="Melf DO-213 AB [SMD]"]
  5k_2 = Resistor [tolerance=±5% resistance=220 package=THT]
  5k_3 = Resistor [tolerance=±5% resistance=220 package=THT]
  10k = Resistor [tolerance=±5% resistance=5k package=THT]
  47k = Resistor [tolerance=±5% resistance=220 package=THT]
  20k = Resistor [tolerance=±5% resistance=220 package=THT]
  - = Pad [width=2 height=2 connect=center]
  + = Pad [width=2 height=2 connect=center]
  ReedPump = Reed switch [package=THT]
  TX = Pad [width=3 height=3 connect=center]
  RX = Pad [width=3 height=3 connect=center]
  TX_2 = Pad [width=3 height=3 connect=center]
  RX_2 = Pad [width=3 height=3 connect=center]

nets:
  N1: ESP8266_NodeMCU_1_0.D0, NPN_2N7000.G, 5k_3.Pin_0
  N2: ESP8266_NodeMCU_1_0.D1, TX_2.pad
  N3: ESP8266_NodeMCU_1_0.D2, 5k_2.Pin_0, 10k.Pin_0
  N4: ESP8266_NodeMCU_1_0.D3, ReedPump.pin_2
  N5: ESP8266_NodeMCU_1_0.GND, BS.G, NPN_2N7000.S, 10k.Pin_1, ReedPump.pin_1
  N6: ESP8266_NodeMCU_1_0.D5, RX.pad
  N7: ESP8266_NodeMCU_1_0.D6, TX.pad
  N8: ESP8266_NodeMCU_1_0.D7, RX_2.pad
  N9: ESP8266_NodeMCU_1_0.Vin, PNP_IRF9540N.drain, D1.cathode
  N10: ESP8266_NodeMCU_1_0.A0, 47k.Pin_1, 20k.Pin_0
  N11: BS.5V, PNP_IRF9540N.source, 5k.Pin_0, Pushbttn.leg1
  N12: PNP_IRF9540N.gate, NPN_2N7000.D, 5k.Pin_1
  N13: Pushbttn.leg0, D1.anode, 5k_2.Pin_1
  N14: 47k.Pin_0, -.pad
  N15: 20k.Pin_1, +.pad

notes:
  Bat
  Mara
  Displ

custom parts:
  NodeMCU V1.0: ESP8266 based NodeMCU
